// Logisim project Ctl_Shift_Add_Sub_Mov.circ as structural Verilog: 1 circuit, main circuit Shift_Add_Sub_Mov
module Shift_Add_Sub_Mov (
  input  Enable,
  input  [15:0] Instruction,
  output [31:0] Imm32,
  output [4:0] Imm5,
  output [2:0] Rd,
  output [2:0] Rm,
  output [2:0] Rn,
  output [3:0] ALU_Opcode,
  output [3:0] Flags_Update_Mask,
  output Carry,
  output Imm32_Enable
);

  wire and_1_out, and_2_out, and_3_out, and_13_out, and_14_out, and_15_out, and_16_out, and_17_out,
       and_18_out, and_19_out, and_20_out, not_1_out, not_2_out, not_3_out, not_4_out, not_5_out, not_6_out;
  wire [2:0] and_4_out, and_7_out, and_21_out, and_24_out, priority_encoder_1_out;

  not not_1 (not_1_out, Instruction[13]);
  not not_2 (not_2_out, Instruction[14]);
  not not_3 (not_3_out, Instruction[15]);
  not not_4 (not_4_out, Instruction[10]);
  and and_1 (and_1_out, not_1_out, not_2_out, not_3_out);
  not not_5 (not_5_out, and_2_out);
  and and_2 (and_2_out, Instruction[11], Instruction[12], not_4_out);
  and and_3 (and_3_out, Instruction[11], Instruction[12]);
  not not_6 (not_6_out, and_1_out);
  and and_4 (and_4_out[0], Instruction[3], not_5_out);
  and and_5 (and_4_out[1], Instruction[4], not_5_out);
  and and_6 (and_4_out[2], Instruction[5], not_5_out);
  and and_7 (and_7_out[0], Instruction[6], and_2_out);
  and and_8 (and_7_out[1], Instruction[7], and_2_out);
  and and_9 (and_7_out[2], Instruction[8], and_2_out);
  and and_10 (Rn[0], Instruction[3], and_3_out);
  and and_11 (Rn[1], Instruction[4], and_3_out);
  and and_12 (Rn[2], Instruction[5], and_3_out);
  and and_13 (and_13_out, ~Instruction[9], ~Instruction[10], ~Instruction[11]);  // AND_Gate
  and and_14 (and_14_out, ~Instruction[9], ~Instruction[10], Instruction[11]);  // AND_Gate
  and and_15 (and_15_out, ~Instruction[9], Instruction[10], ~Instruction[11]);  // AND_Gate
  and and_16 (and_16_out, ~Instruction[9], Instruction[10], Instruction[11], ~Instruction[13]);  // AND_Gate
  and and_17 (and_17_out, ~Instruction[9], Instruction[10], Instruction[11], Instruction[13]);  // AND_Gate
  and and_18 (and_18_out, ~Instruction[9], Instruction[10], Instruction[11]);  // AND_Gate
  and and_19 (and_19_out, Instruction[9], Instruction[10], ~Instruction[11]);  // AND_Gate
  and and_20 (and_20_out, Instruction[9], Instruction[11]);
  and and_21 (and_21_out[0], Instruction[8], not_6_out);
  and and_22 (and_21_out[1], Instruction[9], not_6_out);
  and and_23 (and_21_out[2], Instruction[10], not_6_out);
  and and_24 (and_24_out[0], Instruction[0], and_1_out);
  and and_25 (and_24_out[1], Instruction[1], and_1_out);
  and and_26 (and_24_out[2], Instruction[2], and_1_out);
  Priority_Encoder priority_encoder_1 (
    .in0(and_13_out), .in1(and_14_out), .in2(and_15_out), .in3(and_16_out), .in4(and_17_out),
    .in5(and_18_out), .in6(and_19_out), .in7(and_20_out), .out(priority_encoder_1_out));  // open: en_in, gs, en_out
  assign Rm = and_4_out | and_7_out;  // OR_Gate or_1, 3 bits wide
  Multiplexer #(.enable("false"), .select(3), .width(4)) multiplexer_1 (
    .in0(4'b0010), .in1(4'b0011), .in2(4'b0100), .in3(4'b1011), .in4(4'b1010), .in5(4'b1001), .in6(4'b1011),
    .in7(4'b1010), .out(ALU_Opcode), .sel(priority_encoder_1_out));
  assign Rd = and_21_out | and_24_out;  // OR_Gate or_2, 3 bits wide
  and and_27 (Carry, ~and_16_out, and_17_out, ~and_19_out, and_20_out);  // AND_Gate
  or or_3 (Imm32_Enable, and_18_out, and_19_out, and_20_out);
  Multiplexer #(.enable("false"), .select(3), .width(4)) multiplexer_2 (
    .in0(4'b1110), .in1(4'b1110), .in2(4'b1110), .in3(4'b1111), .in4(4'b1111), .in5(4'b1100), .in6(4'b1111),
    .in7(4'b1111), .out(Flags_Update_Mask), .sel(priority_encoder_1_out));

  assign Imm5 = Instruction[10:6];
  assign Imm32 = {{24{1'b0}}, Instruction[7:0]};

  // Other names for the same wires on the sheet: Instru_8 = Instruction[8]; Instru_9 = Instruction[9];
  //   Instru_10 = Instruction[10]; Instru_0 = Instruction[0]; Instru_1 = Instruction[1]; Instru_2 = Instruction[2];
  //   Instru_3 = Instruction[3]; Instru_4 = Instruction[4]; Instru_5 = Instruction[5]; Instru_6 = Instruction[6];
  //   Instru_7 = Instruction[7]; Instru_11 = Instruction[11]; Instru_12 = Instruction[12];
  //   Instru_13 = Instruction[13]; Instru_14 = Instruction[14]; Instru_15 = Instruction[15]

  // Notes on the sheet:
  //   Not used
  //   LSL
  //   LSR
  //   ASR
  //   ADD
  //   SUB
  //   MOV
  //   ADD
  //   SUB / CMP
  //   Pull output low on Enable = 0
  //   Enable carry for SUB since it is reversed in ALU
  //   only ADD and SUB use Rm
  //   ALU will use Imm32 instead of Rm
endmodule
