// Logisim project BancDeRegistres.circ as structural Verilog: 1 circuit, main circuit banc_de_registre
module banc_de_registre (
  input  [2:0] RegDest,
  input  [31:0] DataIn,
  input  Reset,
  input  Clk,
  input  [2:0] RegA,
  input  [2:0] RegB,
  input  [31:0] in_7,
  output [31:0] Aout,
  output [31:0] Bout
);

  wire demultiplexer_1_out0, demultiplexer_1_out1, demultiplexer_1_out2, demultiplexer_1_out3,
       demultiplexer_1_out4, demultiplexer_1_out5, demultiplexer_1_out6, demultiplexer_1_out7;
  wire [31:0] R0_q, R1_q, R2_q, R3_q, R4_q, R5_q, R6_q, R7_q;

  Demultiplexer #(.enable("false"), .select(3)) demultiplexer_1 (
    .out0(demultiplexer_1_out0), .out1(demultiplexer_1_out1), .out2(demultiplexer_1_out2),
    .out3(demultiplexer_1_out3), .out4(demultiplexer_1_out4), .out5(demultiplexer_1_out5),
    .out6(demultiplexer_1_out6), .out7(demultiplexer_1_out7), .in(1'b1), .sel(RegDest));
  Register #(.width(32)) R0 (.D(DataIn), .en(demultiplexer_1_out0), .clk(Clk), .Q(R0_q), .clr(Reset));
  Register #(.width(32)) R1 (.D(DataIn), .en(demultiplexer_1_out1), .clk(Clk), .Q(R1_q), .clr(Reset));
  Register #(.width(32)) R2 (.D(DataIn), .en(demultiplexer_1_out2), .clk(Clk), .Q(R2_q), .clr(Reset));
  Register #(.width(32)) R3 (.D(DataIn), .en(demultiplexer_1_out3), .clk(Clk), .Q(R3_q), .clr(Reset));
  Register #(.width(32)) R4 (.D(DataIn), .en(demultiplexer_1_out4), .clk(Clk), .Q(R4_q), .clr(Reset));
  Register #(.width(32)) R5 (.D(DataIn), .en(demultiplexer_1_out5), .clk(Clk), .Q(R5_q), .clr(Reset));
  Register #(.width(32)) R6 (.D(DataIn), .en(demultiplexer_1_out6), .clk(Clk), .Q(R6_q), .clr(Reset));
  Register #(.width(32)) R7 (.D(DataIn), .en(demultiplexer_1_out7), .clk(Clk), .Q(R7_q), .clr(Reset));
  Multiplexer #(.enable("false"), .select(3), .width(32)) multiplexer_1 (
    .in0(R0_q), .in1(R1_q), .in2(R2_q), .in3(R3_q), .in4(R4_q), .in5(R5_q), .in6(R6_q), .in7(R7_q),
    .out(Aout), .sel(RegA));
  Multiplexer #(.enable("false"), .select(3), .width(32)) multiplexer_2 (
    .in0(R0_q), .in1(R1_q), .in2(R2_q), .in3(R3_q), .in4(R4_q), .in5(R5_q), .in6(R6_q), .in7(R7_q),
    .out(Bout), .sel(RegB));
endmodule
